# Fritzing sketch alto-proto-bonnet (saved by Fritzing 0.9.2b)
breadboards: 1

parts:
  R2 = Resistor [tolerance=±5% resistance=330 package="0603 [SMD]"]
  R3 = Resistor [tolerance=±5% resistance=330 package="0603 [SMD]"]
  R1 = Resistor [tolerance=±5% resistance=330 package="0603 [SMD]"]
  R5 = Resistor [tolerance=±5% resistance=330 package="0603 [SMD]"]
  R4 = Resistor [tolerance=±5% resistance=330 package="0603 [SMD]"]
  LED1 = LED - 3mm [color="White (4500K)" package="3 mm [THT]"]
  J1 = male pin header, 3 pins [form="♂ (male)"]
  J2 = male pin header, 3 pins [form="♂ (male)"]
  J3 = male pin header, 2 pins [form="♂ (male)"]
  J4 = male pin header, 2 pins [form="♂ (male)"]
  J5 = male pin header, 2 pins [form="♂ (male)"]
  U1 = 5V regulator [chip_label=Regulator package="SIP (Single Inline) [THT]"]
  Part4 = Adafruit Micro USB Breakout [part_number="Adafruit #1833"]

nets:
  N1: R2.Pin_1, J2.pin3
  N2: R3.Pin_1, J3.pin2
  N3: R1.Pin_1, J1.pin3
  N4: R5.Pin_1, LED1.anode
  N5: R4.Pin_1, J4.pin2
  GND: LED1.cathode, J1.pin1, J2.pin1, J3.pin1, J4.pin1, J5.pin2, U1.GND, Part4.GND
  N6: J1.pin2, J2.pin2, J5.pin1, U1.Vin, Part4.VBUS

custom parts:
  Adafruit Micro USB Breakout: Simple but effective - this breakout board has a USB Micro-B connector, with all 5 pins broken out. Great for pairing with a microcontroller with USB support, or adding USB 5V power to a project. We use a micro-AB connector with through-hole shielding pads for an excellent strong connection - it won't rip off by accident! Comes with one fully assembled and tested micro B breakout PCB and a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
